# Fritzing sketch Diagrama (saved by Fritzing 0.9.3b)
breadboards: 1

parts:
  Componente1 = Arduino Uno (Rev3) - ICSP
  LED1 = smd LED [color="Red (633nm)" package="0805 [SMD]"]
  J1 = Piezo Speaker
  Componente2 = Passive Buzzer
  R1 = Resistor [tolerance=±5% resistance=220 package="0805 [SMD]"]

nets:
  N1: Componente1.ICSP_MISO, Componente1.D12/MISO, R1.Pin_1
  GND: Componente1.GND, LED1.cathode, J1.pin1, Componente2.GND
  N2: Componente1.D8, Componente2.S
  N3: Componente1.5V, Componente2.NC
  N4: LED1.anode, R1.Pin_0
